// Logisim project Project.circ as structural Verilog: 7 circuits, main circuit main
module main (
);

  wire [3:0] alu_1_out_4;
  wire [7:0] alu_1_out_3, undriven, undriven_2;

  register register_1 ();  // open: out_1, out_2
  ALU alu_1 (.out_3(alu_1_out_3), .in_1(undriven), .in_2(undriven_2), .out_4(alu_1_out_4));  // open: out_5

  // Notes on the sheet:
  //   PC
  //   ALU
endmodule

module Half_Adder (
  input  in_1,
  input  in_2,
  output out_3,
  output out_4
);

  wire not_1_out, or_1_out;

  or or_1 (or_1_out, in_1, in_2);
  and and_1 (out_4, in_1, in_2);
  and and_2 (out_3, or_1_out, not_1_out);
  not not_1 (not_1_out, out_4);
endmodule

module Full_Adder (
  input  in_1,
  input  in_2,
  input  in_3,
  output out_4,
  output out_5
);

  wire half_adder_1_out_3, half_adder_1_out_4, half_adder_2_out_4;

  Half_Adder half_adder_1 (.in_1(in_1), .in_2(in_2), .out_3(half_adder_1_out_3), .out_4(half_adder_1_out_4));
  Half_Adder half_adder_2 (.in_1(half_adder_1_out_3), .in_2(in_3), .out_3(out_4), .out_4(half_adder_2_out_4));
  or or_1 (out_5, half_adder_2_out_4, half_adder_1_out_4);
endmodule

module Addition (
  input  [7:0] ALU_Left,
  input  [7:0] ALU_Right,
  output [7:0] out_3,
  output Overflow
);

  wire full_adder_1_out_5, full_adder_2_out_5, full_adder_3_out_5, full_adder_4_out_5, full_adder_5_out_5,
       full_adder_6_out_5, half_adder_1_out_4;

  Half_Adder half_adder_1 (.in_1(ALU_Left[0]), .in_2(ALU_Right[0]), .out_3(out_3[0]), .out_4(half_adder_1_out_4));
  Full_Adder full_adder_1 (
    .in_1(half_adder_1_out_4), .in_2(ALU_Right[1]), .in_3(ALU_Left[1]), .out_4(out_3[1]),
    .out_5(full_adder_1_out_5));
  Full_Adder full_adder_2 (
    .in_1(full_adder_1_out_5), .in_2(ALU_Right[2]), .in_3(ALU_Left[2]), .out_4(out_3[2]),
    .out_5(full_adder_2_out_5));
  Full_Adder full_adder_3 (
    .in_1(full_adder_2_out_5), .in_2(ALU_Right[3]), .in_3(ALU_Left[3]), .out_4(out_3[3]),
    .out_5(full_adder_3_out_5));
  Full_Adder full_adder_4 (
    .in_1(full_adder_3_out_5), .in_2(ALU_Right[4]), .in_3(ALU_Left[4]), .out_4(out_3[4]),
    .out_5(full_adder_4_out_5));
  Full_Adder full_adder_5 (
    .in_1(full_adder_4_out_5), .in_2(ALU_Right[5]), .in_3(ALU_Left[5]), .out_4(out_3[5]),
    .out_5(full_adder_5_out_5));
  Full_Adder full_adder_6 (
    .in_1(full_adder_5_out_5), .in_2(ALU_Right[6]), .in_3(ALU_Left[6]), .out_4(out_3[6]),
    .out_5(full_adder_6_out_5));
  Full_Adder full_adder_7 (
    .in_1(full_adder_6_out_5), .in_2(ALU_Right[7]), .in_3(ALU_Left[7]), .out_4(out_3[7]), .out_5(Overflow));

  // Notes on the sheet:
  //   ALU-Out
endmodule

module _2_s_Complement (
  input  [7:0] in_1,
  output [7:0] out_2
);

  wire half_adder_1_out_4, half_adder_2_out_4, half_adder_3_out_4, half_adder_4_out_4, half_adder_5_out_4,
       half_adder_6_out_4, half_adder_7_out_4, not_1_out, not_2_out, not_3_out, not_4_out, not_5_out,
       not_6_out, not_7_out, not_8_out, not_9_out, or_1_out;

  not not_1 (not_1_out, in_1[6]);
  not not_2 (not_2_out, in_1[7]);
  not not_3 (not_3_out, in_1[3]);
  not not_4 (not_4_out, in_1[2]);
  not not_5 (not_5_out, in_1[4]);
  not not_6 (not_6_out, in_1[5]);
  not not_7 (not_7_out, not_9_out);
  not not_8 (not_8_out, in_1[1]);
  not not_9 (not_9_out, in_1[0]);
  or or_1 (or_1_out, not_7_out, not_9_out);
  Half_Adder half_adder_1 (.in_1(or_1_out), .in_2(not_9_out), .out_3(out_2[0]), .out_4(half_adder_1_out_4));
  Half_Adder half_adder_2 (.in_1(half_adder_1_out_4), .in_2(not_8_out), .out_3(out_2[1]), .out_4(half_adder_2_out_4));
  Half_Adder half_adder_3 (.in_1(half_adder_2_out_4), .in_2(not_4_out), .out_3(out_2[2]), .out_4(half_adder_3_out_4));
  Half_Adder half_adder_4 (.in_1(half_adder_3_out_4), .in_2(not_3_out), .out_3(out_2[3]), .out_4(half_adder_4_out_4));
  Half_Adder half_adder_5 (.in_1(half_adder_4_out_4), .in_2(not_5_out), .out_3(out_2[4]), .out_4(half_adder_5_out_4));
  Half_Adder half_adder_6 (.in_1(half_adder_5_out_4), .in_2(not_6_out), .out_3(out_2[5]), .out_4(half_adder_6_out_4));
  Half_Adder half_adder_7 (.in_1(half_adder_6_out_4), .in_2(not_1_out), .out_3(out_2[6]), .out_4(half_adder_7_out_4));
  Half_Adder half_adder_8 (.in_1(half_adder_7_out_4), .in_2(not_2_out), .out_3(out_2[7]));  // open: out_4
endmodule

module ALU (
  input  [7:0] in_1,
  input  [7:0] in_2,
  output [7:0] out_3,
  output [3:0] out_4,
  output out_5
);

  wire [7:0] multiplexer_1_out, n2_s_complement_1_out_2;

  _2_s_Complement u_2_s_complement_1 (.in_1(in_2), .out_2(n2_s_complement_1_out_2));
  Addition addition_1 (.out_3(out_3), .ALU_Left(multiplexer_1_out), .ALU_Right(in_1), .Overflow(out_4[0]));
  Multiplexer #(.width(8)) multiplexer_1 (
    .in0(in_2), .in1(n2_s_complement_1_out_2), .out(multiplexer_1_out), .sel(out_5));  // open: en

  // Notes on the sheet:
  //   ALU-L
  //   ALU-R
  //   Subtraction Selector
  //   Will be made internal
  //   Status
  //   ALU-OUT
  //   Bit 0 - Overflow
endmodule

module register (
  output [7:0] out_1,
  output [7:0] out_2
);

  wire not_1_out, not_2_out, not_3_out, not_4_out, not_5_out, not_6_out, not_7_out, not_8_out;

  not not_1 (not_1_out, out_1[0]);
  not not_2 (not_2_out, out_1[1]);
  not not_3 (not_3_out, out_1[2]);
  not not_4 (not_4_out, out_1[3]);
  not not_5 (not_5_out, out_1[4]);
  not not_6 (not_6_out, out_1[5]);
  not not_7 (not_7_out, out_1[6]);
  not not_8 (not_8_out, out_1[7]);
  S_R_Flip_Flop s_r_ff_1 (.S(out_1[0]), .R(not_1_out), .Q(out_2[0]));  // open: clk, Qn, preset, reset, en
  S_R_Flip_Flop s_r_ff_2 (.S(out_1[1]), .R(not_2_out), .Q(out_2[1]));  // open: clk, Qn, preset, reset, en
  S_R_Flip_Flop s_r_ff_3 (.S(out_1[2]), .R(not_3_out), .Q(out_2[2]));  // open: clk, Qn, preset, reset, en
  S_R_Flip_Flop s_r_ff_4 (.S(out_1[3]), .R(not_4_out), .Q(out_2[3]));  // open: clk, Qn, preset, reset, en
  S_R_Flip_Flop s_r_ff_5 (.S(out_1[4]), .R(not_5_out), .Q(out_2[4]));  // open: clk, Qn, preset, reset, en
  S_R_Flip_Flop s_r_ff_6 (.S(out_1[5]), .R(not_6_out), .Q(out_2[5]));  // open: clk, Qn, preset, reset, en
  S_R_Flip_Flop s_r_ff_7 (.S(out_1[6]), .R(not_7_out), .Q(out_2[6]));  // open: clk, Qn, preset, reset, en
  S_R_Flip_Flop s_r_ff_8 (.S(out_1[7]), .R(not_8_out), .Q(out_2[7]));  // open: clk, Qn, preset, reset, en
endmodule
